// Logisim project Ekran_ver_5_2 (2).circ as structural Verilog: 9 circuits, main circuit контрольная
module \контрольная  (
  input  in_1
);

  wire clock, clock_2_out, reset;
  wire [3:0] sca4, scb4;
  wire [4:0] baty, bx, by, controller, joystick_1_y, kinema_1_leftyout, kinema_1_rightyout, kinema_1_zero,
       videosector_1_ballx_2, videosector_1_bally_2, videosector_1_chipid_2, videosector_1_leftbat_2,
       videosector_1_rightbat_2, videosector_2_ballx_2, videosector_2_bally_2, videosector_2_chipid_2,
       videosector_2_leftbat_2, videosector_2_rightbat_2, videosector_3_ballx_2, videosector_3_bally_2,
       videosector_3_chipid_2, videosector_3_leftbat_2, videosector_3_rightbat_2;
  wire [7:0] sca, scb, vx, vy;
  wire [31:0] videosector_1_out_6, videosector_1_out_7, videosector_1_out_8, videosector_1_out_9,
       videosector_1_out_10, videosector_1_out_11, videosector_1_out_12, videosector_1_out_13,
       videosector_2_out_6, videosector_2_out_7, videosector_2_out_8, videosector_2_out_9,
       videosector_2_out_10, videosector_2_out_11, videosector_2_out_12, videosector_2_out_13,
       videosector_3_out_6, videosector_3_out_7, videosector_3_out_8, videosector_3_out_9,
       videosector_3_out_10, videosector_3_out_11, videosector_3_out_12, videosector_3_out_13,
       videosector_4_out_6, videosector_4_out_7, videosector_4_out_8, videosector_4_out_9,
       videosector_4_out_10, videosector_4_out_11, videosector_4_out_12, videosector_4_out_13;

  Clock clock_1 (.out(clock));
  Button R (.out(reset));
  kinema kinema_1 (
    .clock(clock_2_out), .rightyin(baty), .zero(kinema_1_zero), .ballX(bx), .ballY(by),
    .rightYout(kinema_1_rightyout), .leftYout(kinema_1_leftyout), .leftyin(controller), .longvx(vx),
    .scoreA(sca), .scoreB(scb), .reset(reset), .longvY(vy), .gameType(in_1));
  Clock #(.highDuration(2), .lowDuration(2)) clock_2 (.out(clock_2_out));
  Hex_Digit_Display hex_digit_display_1 (.value(sca4));  // open: dp
  counter counter_1 (.\input (sca), .out_2(sca4));
  Joystick #(.bits(5)) joystick_1 (.y(joystick_1_y));  // open: x
  assign controller = ~joystick_1_y;  // NOT_Gate not_1, 5 bits wide
  DotMatrix #(.matrixcols(32), .matrixrows(32)) dotmatrix_1 (
    .col0(videosector_1_out_6), .col1(videosector_1_out_7), .col2(videosector_1_out_8),
    .col3(videosector_1_out_9), .col4(videosector_1_out_10), .col5(videosector_1_out_11),
    .col6(videosector_1_out_12), .col7(videosector_1_out_13), .col8(videosector_2_out_6),
    .col9(videosector_2_out_7), .col10(videosector_2_out_8), .col11(videosector_2_out_9),
    .col12(videosector_2_out_10), .col13(videosector_2_out_11), .col14(videosector_2_out_12),
    .col15(videosector_2_out_13), .col16(videosector_3_out_6), .col17(videosector_3_out_7),
    .col18(videosector_3_out_8), .col19(videosector_3_out_9), .col20(videosector_3_out_10),
    .col21(videosector_3_out_11), .col22(videosector_3_out_12), .col23(videosector_3_out_13),
    .col24(videosector_4_out_6), .col25(videosector_4_out_7), .col26(videosector_4_out_8),
    .col27(videosector_4_out_9), .col28(videosector_4_out_10), .col29(videosector_4_out_11),
    .col30(videosector_4_out_12), .col31(videosector_4_out_13));
  VideoSector videosector_1 (
    .BallY(by), .BallX(bx), .LeftBat(kinema_1_rightyout), .rightBat(kinema_1_leftyout),
    .ChipId(kinema_1_zero), .BallY_2(videosector_1_bally_2), .BallX_2(videosector_1_ballx_2),
    .LeftBat_2(videosector_1_leftbat_2), .rightBat_2(videosector_1_rightbat_2),
    .ChipId_2(videosector_1_chipid_2), .out_6(videosector_1_out_6), .out_7(videosector_1_out_7),
    .out_8(videosector_1_out_8), .out_9(videosector_1_out_9), .out_10(videosector_1_out_10),
    .out_11(videosector_1_out_11), .out_12(videosector_1_out_12), .out_13(videosector_1_out_13));
  VideoSector videosector_2 (
    .BallY(videosector_1_bally_2), .BallX(videosector_1_ballx_2), .LeftBat(videosector_1_leftbat_2),
    .rightBat(videosector_1_rightbat_2), .ChipId(videosector_1_chipid_2), .BallY_2(videosector_2_bally_2),
    .BallX_2(videosector_2_ballx_2), .LeftBat_2(videosector_2_leftbat_2),
    .rightBat_2(videosector_2_rightbat_2), .ChipId_2(videosector_2_chipid_2), .out_6(videosector_2_out_6),
    .out_7(videosector_2_out_7), .out_8(videosector_2_out_8), .out_9(videosector_2_out_9),
    .out_10(videosector_2_out_10), .out_11(videosector_2_out_11), .out_12(videosector_2_out_12),
    .out_13(videosector_2_out_13));
  VideoSector videosector_3 (
    .BallY(videosector_2_bally_2), .BallX(videosector_2_ballx_2), .LeftBat(videosector_2_leftbat_2),
    .rightBat(videosector_2_rightbat_2), .ChipId(videosector_2_chipid_2), .BallY_2(videosector_3_bally_2),
    .BallX_2(videosector_3_ballx_2), .LeftBat_2(videosector_3_leftbat_2),
    .rightBat_2(videosector_3_rightbat_2), .ChipId_2(videosector_3_chipid_2), .out_6(videosector_3_out_6),
    .out_7(videosector_3_out_7), .out_8(videosector_3_out_8), .out_9(videosector_3_out_9),
    .out_10(videosector_3_out_10), .out_11(videosector_3_out_11), .out_12(videosector_3_out_12),
    .out_13(videosector_3_out_13));
  VideoSector videosector_4 (
    .BallY(videosector_3_bally_2), .BallX(videosector_3_ballx_2), .LeftBat(videosector_3_leftbat_2),
    .rightBat(videosector_3_rightbat_2), .ChipId(videosector_3_chipid_2), .out_6(videosector_4_out_6),
    .out_7(videosector_4_out_7), .out_8(videosector_4_out_8), .out_9(videosector_4_out_9),
    .out_10(videosector_4_out_10), .out_11(videosector_4_out_11), .out_12(videosector_4_out_12),
    .out_13(videosector_4_out_13));  // open: BallY_2, BallX_2, LeftBat_2, rightBat_2, ChipId_2
  Hex_Digit_Display hex_digit_display_2 (.value(scb4));  // open: dp
  counter counter_2 (.\input (scb), .out_2(scb4));
  Ryzen_Core_I9 ryzen_core_i9_1 (.clock(clock), .BAATY(baty), .VX(vx), .BX(bx), .BY(by), .VY(vy));

  // Notes on the sheet:
  //   Wanna reset?
  //    Sony DualSense Elite Controller
endmodule

module levelUpedVideoChip (
  input  [4:0] ballY,
  input  [4:0] ballX,
  input  [4:0] laftBat,
  input  [4:0] rightBat,
  input  [4:0] chipID,
  output [31:0] out_6,
  output [4:0] ballY_2,
  output [4:0] ballX_2,
  output [4:0] laftBat_2,
  output [4:0] rightBat_2,
  output [4:0] chipID_2
);

  wire nor_3_out;
  wire [1:0] nor_1_out;
  wire [4:0] xor_1_out, xor_2_out, xor_3_out;
  wire [31:0] _1, _2, BALL, rocket, shifter_1_out, shifter_2_out, shifter_3_out;

  assign xor_1_out = 5'b00011 ^ chipID;  // XOR_Gate xor_1, 5 bits wide
  assign xor_2_out = 5'b11101 ^ chipID;  // XOR_Gate xor_2, 5 bits wide
  nor nor_1 (nor_1_out[0], xor_1_out[0], xor_1_out[1], xor_1_out[2], xor_1_out[3], xor_1_out[4]);
  nor nor_2 (nor_1_out[1], xor_2_out[0], xor_2_out[1], xor_2_out[2], xor_2_out[3], xor_2_out[4]);
  assign out_6 = BALL | rocket;  // OR_Gate or_1, 32 bits wide
  Shifter #(.width(32)) shifter_1 (.in(32'h1), .\dist (ballY), .out(shifter_1_out));
  assign xor_3_out = ballX ^ chipID;  // XOR_Gate xor_3, 5 bits wide
  Multiplexer #(.width(32), .enable("false")) multiplexer_1 (
    .in0({32{1'b0}}), .in1(shifter_1_out), .out(BALL), .sel(nor_3_out));
  nor nor_3 (nor_3_out, xor_3_out[0], xor_3_out[1], xor_3_out[2], xor_3_out[3], xor_3_out[4]);
  Adder #(.width(5)) adder_1 (.a(chipID), .b(5'b00001), .out(chipID_2));  // open: cin, cout
  Multiplexer #(.select(2), .width(32), .enable("false")) multiplexer_2 (
    .in0({32{1'b0}}), .in1(_2), .in2(_1), .out(rocket), .sel(nor_1_out));  // open: in3
  \добавлялкаСоседейдляРакеток  \u_добавлялкасоседейдляракеток_1  (.in_1(shifter_2_out), .out_2(_1));
  Shifter #(.width(32)) shifter_2 (.in(32'h1), .\dist (laftBat), .out(shifter_2_out));
  Shifter #(.width(32)) shifter_3 (.in(32'h1), .\dist (rightBat), .out(shifter_3_out));
  \добавлялкаСоседейдляРакеток  \u_добавлялкасоседейдляракеток_2  (.in_1(shifter_3_out), .out_2(_2));

  assign ballX_2 = ballX;
  assign ballY_2 = ballY;
  assign laftBat_2 = laftBat;
  assign rightBat_2 = rightBat;

  // Other names for the same wires on the sheet: BX[4:0] = ballX; BY[4:0] = ballY; ID[4:0] = chipID;
  //   LB[4:0] = laftBat; RB[4:0] = rightBat
endmodule

// RTX 6900XT
module VideoSector (
  input  [4:0] BallY,
  input  [4:0] BallX,
  input  [4:0] LeftBat,
  input  [4:0] rightBat,
  input  [4:0] ChipId,
  output [31:0] out_6,
  output [31:0] out_7,
  output [31:0] out_8,
  output [31:0] out_9,
  output [31:0] out_10,
  output [31:0] out_11,
  output [31:0] out_12,
  output [31:0] out_13,
  output [4:0] BallY_2,
  output [4:0] BallX_2,
  output [4:0] LeftBat_2,
  output [4:0] rightBat_2,
  output [4:0] ChipId_2
);

  wire [4:0] levelupedvideochip_1_ballx_2, levelupedvideochip_1_bally_2, levelupedvideochip_1_chipid_2,
       levelupedvideochip_1_laftbat_2, levelupedvideochip_1_rightbat_2, levelupedvideochip_2_ballx_2,
       levelupedvideochip_2_bally_2, levelupedvideochip_2_chipid_2, levelupedvideochip_2_laftbat_2,
       levelupedvideochip_2_rightbat_2, levelupedvideochip_3_ballx_2, levelupedvideochip_3_bally_2,
       levelupedvideochip_3_chipid_2, levelupedvideochip_3_laftbat_2, levelupedvideochip_3_rightbat_2,
       levelupedvideochip_4_ballx_2, levelupedvideochip_4_bally_2, levelupedvideochip_4_chipid_2,
       levelupedvideochip_4_laftbat_2, levelupedvideochip_4_rightbat_2, levelupedvideochip_5_ballx_2,
       levelupedvideochip_5_bally_2, levelupedvideochip_5_chipid_2, levelupedvideochip_5_laftbat_2,
       levelupedvideochip_5_rightbat_2, levelupedvideochip_6_ballx_2, levelupedvideochip_6_bally_2,
       levelupedvideochip_6_chipid_2, levelupedvideochip_6_laftbat_2, levelupedvideochip_6_rightbat_2,
       levelupedvideochip_7_ballx_2, levelupedvideochip_7_bally_2, levelupedvideochip_7_chipid_2,
       levelupedvideochip_7_laftbat_2, levelupedvideochip_7_rightbat_2;

  levelUpedVideoChip levelupedvideochip_1 (
    .ballY(BallY), .ballX(BallX), .laftBat(LeftBat), .rightBat(rightBat), .chipID(ChipId), .out_6(out_6),
    .ballY_2(levelupedvideochip_1_bally_2), .ballX_2(levelupedvideochip_1_ballx_2),
    .laftBat_2(levelupedvideochip_1_laftbat_2), .rightBat_2(levelupedvideochip_1_rightbat_2),
    .chipID_2(levelupedvideochip_1_chipid_2));
  levelUpedVideoChip levelupedvideochip_2 (
    .ballY(levelupedvideochip_1_bally_2), .ballX(levelupedvideochip_1_ballx_2),
    .laftBat(levelupedvideochip_1_laftbat_2), .rightBat(levelupedvideochip_1_rightbat_2),
    .chipID(levelupedvideochip_1_chipid_2), .out_6(out_7), .ballY_2(levelupedvideochip_2_bally_2),
    .ballX_2(levelupedvideochip_2_ballx_2), .laftBat_2(levelupedvideochip_2_laftbat_2),
    .rightBat_2(levelupedvideochip_2_rightbat_2), .chipID_2(levelupedvideochip_2_chipid_2));
  levelUpedVideoChip levelupedvideochip_3 (
    .ballY(levelupedvideochip_4_bally_2), .ballX(levelupedvideochip_4_ballx_2),
    .laftBat(levelupedvideochip_4_laftbat_2), .rightBat(levelupedvideochip_4_rightbat_2),
    .chipID(levelupedvideochip_4_chipid_2), .out_6(out_10), .ballY_2(levelupedvideochip_3_bally_2),
    .ballX_2(levelupedvideochip_3_ballx_2), .laftBat_2(levelupedvideochip_3_laftbat_2),
    .rightBat_2(levelupedvideochip_3_rightbat_2), .chipID_2(levelupedvideochip_3_chipid_2));
  levelUpedVideoChip levelupedvideochip_4 (
    .ballY(levelupedvideochip_5_bally_2), .ballX(levelupedvideochip_5_ballx_2),
    .laftBat(levelupedvideochip_5_laftbat_2), .rightBat(levelupedvideochip_5_rightbat_2),
    .chipID(levelupedvideochip_5_chipid_2), .out_6(out_9), .ballY_2(levelupedvideochip_4_bally_2),
    .ballX_2(levelupedvideochip_4_ballx_2), .laftBat_2(levelupedvideochip_4_laftbat_2),
    .rightBat_2(levelupedvideochip_4_rightbat_2), .chipID_2(levelupedvideochip_4_chipid_2));
  levelUpedVideoChip levelupedvideochip_5 (
    .ballY(levelupedvideochip_2_bally_2), .ballX(levelupedvideochip_2_ballx_2),
    .laftBat(levelupedvideochip_2_laftbat_2), .rightBat(levelupedvideochip_2_rightbat_2),
    .chipID(levelupedvideochip_2_chipid_2), .out_6(out_8), .ballY_2(levelupedvideochip_5_bally_2),
    .ballX_2(levelupedvideochip_5_ballx_2), .laftBat_2(levelupedvideochip_5_laftbat_2),
    .rightBat_2(levelupedvideochip_5_rightbat_2), .chipID_2(levelupedvideochip_5_chipid_2));
  levelUpedVideoChip levelupedvideochip_6 (
    .ballY(levelupedvideochip_3_bally_2), .ballX(levelupedvideochip_3_ballx_2),
    .laftBat(levelupedvideochip_3_laftbat_2), .rightBat(levelupedvideochip_3_rightbat_2),
    .chipID(levelupedvideochip_3_chipid_2), .out_6(out_11), .ballY_2(levelupedvideochip_6_bally_2),
    .ballX_2(levelupedvideochip_6_ballx_2), .laftBat_2(levelupedvideochip_6_laftbat_2),
    .rightBat_2(levelupedvideochip_6_rightbat_2), .chipID_2(levelupedvideochip_6_chipid_2));
  levelUpedVideoChip levelupedvideochip_7 (
    .ballY(levelupedvideochip_6_bally_2), .ballX(levelupedvideochip_6_ballx_2),
    .laftBat(levelupedvideochip_6_laftbat_2), .rightBat(levelupedvideochip_6_rightbat_2),
    .chipID(levelupedvideochip_6_chipid_2), .out_6(out_12), .ballY_2(levelupedvideochip_7_bally_2),
    .ballX_2(levelupedvideochip_7_ballx_2), .laftBat_2(levelupedvideochip_7_laftbat_2),
    .rightBat_2(levelupedvideochip_7_rightbat_2), .chipID_2(levelupedvideochip_7_chipid_2));
  levelUpedVideoChip levelupedvideochip_8 (
    .ballY(levelupedvideochip_7_bally_2), .ballX(levelupedvideochip_7_ballx_2),
    .laftBat(levelupedvideochip_7_laftbat_2), .rightBat(levelupedvideochip_7_rightbat_2),
    .chipID(levelupedvideochip_7_chipid_2), .out_6(out_13), .ballY_2(BallY_2), .ballX_2(BallX_2),
    .laftBat_2(LeftBat_2), .rightBat_2(rightBat_2), .chipID_2(ChipId_2));
endmodule

module \добавлялкаСоседейдляРакеток  (
  input  [31:0] in_1,
  output [31:0] out_2
);

  wire [31:0] adder_1_out, shifter_1_out, shifter_2_out;

  Shifter #(.width(32), .shift("lr")) shifter_1 (.in(in_1), .\dist (5'b00001), .out(shifter_1_out));
  Adder #(.width(32)) adder_1 (.a(in_1), .b(shifter_1_out), .out(adder_1_out));  // open: cin, cout
  Shifter #(.width(32)) shifter_2 (.in(in_1), .\dist (5'b00001), .out(shifter_2_out));
  Adder #(.width(32)) adder_2 (.a(adder_1_out), .b(shifter_2_out), .out(out_2));  // open: cin, cout
endmodule

// good boy
module kinema (
  input  [4:0] leftyin,
  input  clock,
  input  [4:0] rightyin,
  input  gameType,
  input  reset,
  output [7:0] longvx,
  output [7:0] longvY,
  output [7:0] scoreA,
  output [7:0] scoreB,
  output [4:0] zero,
  output [4:0] ballX,
  output [4:0] ballY,
  output [4:0] rightYout,
  output [4:0] leftYout
);

  wire adder_4_cout, adder_5_cout, adder_9_cout, adder_10_cout, and_3_out, Bcontact, comparator_1_eq,
       comparator_2_gt, comparator_3_eq, comparator_4_eq, comparator_5_eq, comparator_6_eq, comparator_7_eq,
       comparator_7_gt, comparator_7_lt, FullReset, hitA, hitB, inrange_1_sharearrow, inrange_2_sharearrow,
       LBcontact, not_1_out, not_2_out, not_3_out, not_4_out, not_5_out, not_6_out, not_7_out, not_10_out,
       not_11_out, not_12_out, or_2_out, or_3_out, or_6_out, or_7_out, or_8_out, or_9_out, RBcontact,
       reset_t, xrefl, yrefl;
  wire [1:0] random_1_out;
  wire [2:0] adder_11_out, adder_12_out, addToY, addToY_prime, bit_extender_1_out, bit_extender_2_out,
       controlled_buffer_1_out, multiplexer_6_out, multiplexer_7_out, multiplexer_8_out, multiplexer_9_out,
       multiplexer_10_out, reflect_1_newv, reflect_2_newv, xreg, yreg;
  wire [4:0] multiplexer_1_out;
  wire [7:0] adder_1_out, adder_2_out, adder_3_out, adder_6_out, adder_7_out, adder_8_out, multiplexer_2_out,
       multiplexer_3_out, register_4_q, register_5_q;

  not not_1 (not_1_out, LBcontact);
  not not_2 (not_2_out, RBcontact);
  not not_3 (not_3_out, longvx[7]);
  Adder adder_1 (.a({ballX, xreg}), .b({{6{longvx[7]}}, longvx[1:0]}), .out(adder_1_out));  // open: cin, cout
  Adder adder_2 (.a({ballY, yreg}), .b({{6{longvY[7]}}, longvY[1:0]}), .out(adder_2_out));  // open: cin, cout
  Multiplexer #(.width(5), .enable("false")) multiplexer_1 (
    .in0(rightyin), .in1(5'b01111), .out(multiplexer_1_out), .sel(reset_t));
  and and_1 (hitA, xrefl, not_1_out, longvx[7]);
  and and_2 (hitB, xrefl, not_2_out, not_3_out);
  or or_1 (Bcontact, RBcontact, LBcontact);
  Multiplexer #(.width(8), .enable("false")) multiplexer_2 (
    .in0(adder_1_out), .in1(8'h80), .out(multiplexer_2_out), .sel(reset_t));
  or or_2 (or_2_out, and_3_out, reset_t);
  Multiplexer #(.width(8), .enable("false")) multiplexer_3 (
    .in0(adder_2_out), .in1(8'h80), .out(multiplexer_3_out), .sel(reset_t));
  or or_3 (or_3_out, not_4_out, reset_t);
  Register #(.width(5)) register_1 (.D(multiplexer_1_out), .en(1'b1), .Q(rightYout), .clk(clock));  // open: clr
  Comparator comparator_1 (.a(scoreA), .b(8'h9), .eq(comparator_1_eq));  // open: gt, lt
  Comparator comparator_2 (.a(scoreB), .b(8'h9), .gt(comparator_2_gt), .eq(comparator_2_gt));  // open: lt
  Register register_2 (.D(multiplexer_2_out), .en(or_2_out), .Q({ballX, xreg}), .clk(clock));  // open: clr
  and and_3 (and_3_out, not_5_out, not_6_out);
  Register register_3 (.D(multiplexer_3_out), .en(or_3_out), .Q({ballY, yreg}), .clk(clock));  // open: clr
  not not_4 (not_4_out, yrefl);
  or or_4 (reset_t, hitA, FullReset, hitB);
  or or_5 (FullReset, comparator_1_eq, reset, comparator_2_gt);
  not not_5 (not_5_out, xrefl);
  not not_6 (not_6_out, Bcontact);
  Adder adder_3 (.a({ballX, xreg}), .b(8'he4), .out(adder_3_out));  // open: cin, cout
  Adder adder_4 (.a(adder_3_out), .b({{6{longvx[7]}}, longvx[1:0]}), .cout(adder_4_cout));  // open: out, cin
  not not_7 (not_7_out, comparator_3_eq);
  Comparator #(.width(1)) comparator_3 (.a(adder_4_cout), .b(longvx[7]), .eq(comparator_3_eq));  // open: gt, lt
  inrange inrange_1 (.Yball(ballY), .ybat(leftyin), .out_3(addToY), .shareArrow(inrange_1_sharearrow));
  Register register_4 (.D(scoreA), .en(hitB), .Q(register_4_q), .clk(clock), .clr(FullReset));
  Register register_5 (.D(scoreB), .en(hitA), .Q(register_5_q), .clk(clock), .clr(FullReset));
  Adder adder_5 (.a({ballX, xreg}), .b({{6{longvx[7]}}, longvx[1:0]}), .cout(adder_5_cout));  // open: out, cin
  and and_4 (LBcontact, not_7_out, inrange_1_sharearrow);
  Adder adder_6 (.a(register_4_q), .b(8'h1), .out(adder_6_out));  // open: cin, cout
  Adder adder_7 (.a(register_5_q), .b(8'h1), .out(adder_7_out));  // open: cin, cout
  Comparator #(.width(1)) comparator_4 (.a(adder_5_cout), .b(longvx[7]), .eq(comparator_4_eq));  // open: gt, lt
  not not_8 (xrefl, comparator_4_eq);
  Multiplexer #(.width(8), .enable("false")) multiplexer_4 (
    .in0(register_4_q), .in1(adder_6_out), .out(scoreA), .sel(hitB));
  Multiplexer #(.width(8), .enable("false")) multiplexer_5 (
    .in0(register_5_q), .in1(adder_7_out), .out(scoreB), .sel(hitA));
  Adder adder_8 (.a({ballX, xreg}), .b(8'h1c), .out(adder_8_out));  // open: cin, cout
  Adder adder_9 (.a({ballY, yreg}), .b({{6{longvY[7]}}, longvY[1:0]}), .cout(adder_9_cout));  // open: out, cin
  Adder adder_10 (.a(adder_8_out), .b({{6{longvx[7]}}, longvx[1:0]}), .cout(adder_10_cout));  // open: out, cin
  not not_9 (yrefl, comparator_5_eq);
  Comparator #(.width(1)) comparator_5 (.a(adder_9_cout), .b(longvY[7]), .eq(comparator_5_eq));  // open: gt, lt
  not not_10 (not_10_out, comparator_6_eq);
  Comparator #(.width(1)) comparator_6 (.a(adder_10_cout), .b(longvx[7]), .eq(comparator_6_eq));  // open: gt, lt
  inrange inrange_2 (.Yball(ballY), .ybat(rightyin), .out_3(addToY_prime), .shareArrow(inrange_2_sharearrow));
  assign bit_extender_1_out = {{2{1'b0}}, not_11_out};  // Bit_Extender bit_extender_1
  not not_11 (not_11_out, gameType);
  assign controlled_buffer_1_out = or_6_out ? bit_extender_2_out : 3'bz;  // Controlled_Buffer controlled_buffer_1
  Random #(.width(2)) random_1 (.clk(reset_t), .next(reset_t), .out(random_1_out));  // open: clr
  assign bit_extender_2_out = {{1{1'b0}}, random_1_out};  // Bit_Extender bit_extender_2
  and and_5 (RBcontact, not_10_out, inrange_2_sharearrow);
  reflect reflect_1 (.oldv({longvY[7], longvY[1:0]}), .newv(reflect_1_newv));
  assign controlled_buffer_1_out = comparator_7_gt ? 3'b100 : 3'bz;  // Controlled_Buffer controlled_buffer_2
  Comparator #(.width(3)) comparator_7 (
    .a(bit_extender_2_out), .b(3'b011), .gt(comparator_7_gt), .eq(comparator_7_eq), .lt(comparator_7_lt));
  or or_6 (or_6_out, comparator_7_eq, comparator_7_lt);
  Multiplexer #(.select(2), .width(3), .disabled(0), .enable("false")) multiplexer_6 (
    .in0(3'b000), .in1(addToY), .in2(addToY_prime), .out(multiplexer_6_out), .sel({RBcontact, LBcontact}));  // open: in3
  Multiplexer #(.width(3), .enable("false")) multiplexer_7 (
    .in0({longvY[7], longvY[1:0]}), .in1(reflect_1_newv), .out(multiplexer_7_out), .sel(yrefl));
  Multiplexer #(.width(3), .enable("false")) multiplexer_8 (
    .in0(multiplexer_7_out), .in1(adder_11_out), .out(multiplexer_8_out), .sel(reset_t));
  Adder #(.width(3)) adder_11 (
    .a(bit_extender_1_out), .b(controlled_buffer_1_out), .out(adder_11_out));  // open: cin, cout
  reflect reflect_2 (.oldv({longvx[7], longvx[1:0]}), .newv(reflect_2_newv));
  Adder #(.width(3)) adder_12 (.a(multiplexer_6_out), .b(multiplexer_8_out), .out(adder_12_out));  // open: cin, cout
  Multiplexer #(.width(3), .enable("false")) multiplexer_9 (
    .in0(reflect_2_newv), .in1(3'b110), .out(multiplexer_9_out), .sel(reset_t));
  not not_12 (not_12_out, gameType);
  Multiplexer #(.width(3), .enable("false")) multiplexer_10 (
    .in0(adder_12_out), .in1(multiplexer_8_out), .out(multiplexer_10_out), .sel(not_12_out));
  or or_7 (or_7_out, reset_t, yrefl, or_9_out);
  or or_8 (or_8_out, reset_t, Bcontact, xrefl);
  Register #(.width(3)) register_6 (
    .D(multiplexer_10_out), .en(or_7_out), .Q({longvY[7], longvY[1:0]}), .clk(clock));  // open: clr
  or or_9 (or_9_out, LBcontact, RBcontact);
  Register #(.width(3)) register_7 (
    .D(multiplexer_9_out), .en(or_8_out), .Q({longvx[7], longvx[1:0]}), .clk(clock));  // open: clr

  assign leftYout = leftyin;
  assign longvx[6:2] = {5{longvx[7]}};
  assign longvY[6:2] = {5{longvY[7]}};
  assign zero = {5{1'b0}};

  // Other names for the same wires on the sheet: xreg[7:3] = ballX; yreg[7:3] = ballY;
  //   vx[2:0] = {longvx[7], longvx[1:0]}; vxy[5:0] = {longvY[7], longvY[1:0], longvx[7], longvx[1:0]};
  //   vxneg = longvx[7]; vy[2:0] = {longvY[7], longvY[1:0]}; vyneg = longvY[7]; rightYreg[4:0] = rightYout

  // Notes on the sheet:
  //   Inputs
  //   Outputs
  //   Combinational
  //   Behavior
endmodule

module reflect (
  input  [2:0] oldv,
  output [2:0] newv
);

  wire comparator_1_eq, comparator_2_eq, comparator_2_gt;
  wire [2:0] adder_1_out, newVal, not_1_out, not_2_out, oldVal;

  assign not_1_out = ~oldv;  // NOT_Gate not_1, 3 bits wide
  Comparator #(.width(3)) comparator_1 (.a(oldv), .b(3'b100), .eq(comparator_1_eq));  // open: gt, lt
  Adder #(.width(3)) adder_1 (.a(not_1_out), .b(3'b001), .out(adder_1_out));  // open: cin, cout
  Multiplexer #(.width(3), .enable("false")) multiplexer_1 (
    .in0(adder_1_out), .in1(not_2_out), .out(newv), .sel(comparator_1_eq));
  assign not_2_out = ~oldv;  // NOT_Gate not_2, 3 bits wide
  Comparator #(.width(3)) comparator_2 (
    .a(oldVal), .b(3'b100), .gt(comparator_2_gt), .eq(comparator_2_eq));  // open: lt
  assign newVal = comparator_2_eq ? 3'b101 : 3'bz;  // Controlled_Buffer controlled_buffer_1
  assign newVal = comparator_2_gt ? 3'b100 : 3'bz;  // Controlled_Buffer controlled_buffer_2
endmodule

module inrange (
  input  [4:0] Yball,
  input  [4:0] ybat,
  output [2:0] out_3,
  output shareArrow
);

  wire nor_1_out;
  wire [1:0] nor_2_out;
  wire [4:0] xor_1_out, xor_2_out, xor_3_out, ybatdec, ybatinc;

  assign xor_1_out = Yball ^ ybat;  // XOR_Gate xor_1, 5 bits wide
  assign xor_2_out = Yball ^ ybatinc;  // XOR_Gate xor_2, 5 bits wide
  assign xor_3_out = Yball ^ ybatdec;  // XOR_Gate xor_3, 5 bits wide
  Adder #(.width(5)) adder_1 (.a(ybat), .b(5'b00001), .out(ybatinc));  // open: cin, cout
  Subtractor #(.width(5)) subtractor_1 (.a(ybat), .b(5'b00001), .out(ybatdec));  // open: bin, bout
  Multiplexer #(.select(2), .width(3), .enable("false")) multiplexer_1 (
    .in0(3'b000), .in1(3'b001), .in2(3'b111), .out(out_3), .sel(nor_2_out));  // open: in3
  nor nor_1 (nor_1_out, xor_1_out[0], xor_1_out[1], xor_1_out[2], xor_1_out[3], xor_1_out[4]);
  nor nor_2 (nor_2_out[0], xor_2_out[0], xor_2_out[1], xor_2_out[2], xor_2_out[3], xor_2_out[4]);
  nor nor_3 (nor_2_out[1], xor_3_out[0], xor_3_out[1], xor_3_out[2], xor_3_out[3], xor_3_out[4]);
  or or_1 (shareArrow, nor_1_out, nor_2_out[0], nor_2_out[1]);
endmodule

module counter (
  input  [7:0] \input ,
  output [3:0] out_2
);


  assign out_2 = \input [3:0];
endmodule

// Ryzen r9 11900k
module Ryzen_Core_I9 (
  input  clock,
  input  [7:0] VX,
  input  [7:0] VY,
  input  [4:0] BX,
  input  [4:0] BY,
  output [4:0] BAATY
);

  wire and_1_out, cdm_8_mark5_1_p1, cdm_8_mark5_1_p2, cdm_8_mark5_1_p4, cdm_8_mark5_1_p5, cdm_8_mark5_1_p6,
       cdm_8_mark5_1_p7, comparator_1_eq, comparator_2_eq, comparator_3_eq, comparator_4_eq, comparator_5_eq,
       not_1_out;
  wire [7:0] adr, BX_t, BY_t, cdm_8_mark5_1_p9, cdm_8_mark5_1_p10, controlled_buffer_2_out,
       multiplexer_2_out, multiplexer_3_out, multiplexer_4_out, ram_1_data;
  wire [7:5] register_1_q;

  // Probe on cdm_8_mark5_1_p2
  // Probe on cdm_8_mark5_1_p1
  // Probe on cdm_8_mark5_1_p4
  // Probe on cdm_8_mark5_1_p5
  Comparator comparator_1 (.a(adr), .b(8'hfb), .eq(comparator_1_eq));  // open: gt, lt
  Comparator comparator_2 (.a(adr), .b(8'hfc), .eq(comparator_2_eq));  // open: gt, lt
  Comparator comparator_3 (.a(adr), .b(8'hfd), .eq(comparator_3_eq));  // open: gt, lt
  Comparator comparator_4 (.a(adr), .b(8'hfe), .eq(comparator_4_eq));  // open: gt, lt
  // CdM_8_mark5 cdm_8_mark5_1: pin names not known; wires that end beside it: cdm_8_mark5_1_p1, cdm_8_mark5_1_p2, clock, cdm_8_mark5_1_p4, cdm_8_mark5_1_p5, cdm_8_mark5_1_p6, cdm_8_mark5_1_p7, adr, cdm_8_mark5_1_p9, cdm_8_mark5_1_p10, VY
  Multiplexer #(.width(8), .enable("false")) multiplexer_1 (
    .in0(multiplexer_3_out), .in1(VX), .out(cdm_8_mark5_1_p10), .sel(comparator_1_eq));
  Multiplexer #(.width(8), .enable("false")) multiplexer_2 (
    .in0(multiplexer_4_out), .in1(BX_t), .out(multiplexer_2_out), .sel(comparator_3_eq));
  Multiplexer #(.width(8), .enable("false")) multiplexer_3 (
    .in0(multiplexer_2_out), .in1(VY), .out(multiplexer_3_out), .sel(comparator_2_eq));
  Multiplexer #(.width(8), .enable("false")) multiplexer_4 (
    .in0(controlled_buffer_2_out), .in1(BY_t), .out(multiplexer_4_out), .sel(comparator_4_eq));
  RAM ram_1 (.addr(adr), .data(ram_1_data), .sel(cdm_8_mark5_1_p6), .clk(clock), .ld(cdm_8_mark5_1_p7));  // open: clr
  not not_1 (not_1_out, cdm_8_mark5_1_p7);
  and and_1 (and_1_out, ~cdm_8_mark5_1_p7, cdm_8_mark5_1_p6, comparator_5_eq);  // AND_Gate
  assign BX_t = {{3{1'b0}}, BX};  // Bit_Extender bit_extender_1
  assign BY_t = {{3{1'b0}}, BY};  // Bit_Extender bit_extender_2
  assign ram_1_data = not_1_out ? cdm_8_mark5_1_p9 : 8'bz;  // Controlled_Buffer controlled_buffer_1
  assign controlled_buffer_2_out = cdm_8_mark5_1_p7 ? ram_1_data : 8'bz;  // Controlled_Buffer controlled_buffer_2
  Register register_1 (.D(cdm_8_mark5_1_p9), .en(and_1_out), .Q({register_1_q, BAATY}), .clk(clock));  // open: clr
  Comparator comparator_5 (.a(adr), .b({8{1'b1}}), .eq(comparator_5_eq));  // open: gt, lt
endmodule
